# Fritzing sketch progetto_federica_vs1 (saved by Fritzing 0.9.2b)
breadboards: 1

parts:
  Componente1 = Arduino Uno (Rev3)
  J1 = Piezo Speaker
  S1 = Pushbutton [package="[THT]"]
  S2 = Pushbutton [package="[THT]"]
  R1 = Resistor [tolerance=±5% resistance=10k package=THT]
  R3 = Resistor [tolerance=±5% resistance=220 package=THT]
  LED1 = smd LED [color="Red (633nm)" package="1206 [SMD]"]
  R4 = Resistor [tolerance=±5% resistance=10k package=THT]

nets:
  N1: Componente1.D9_PWM, R3.Pin_0
  N2: Componente1.D11_PWM/MOSI, S1.Pin_1, S1.Pin_2, R1.Pin_0
  N3: Componente1.D12/MISO, J1.pin2
  N4: J1.pin1, R1.Pin_1, R4.Pin_1
  N5: S1.Pin_3, S1.Pin_4, S2.Pin_3, S2.Pin_4
  N6: S2.Pin_1, S2.Pin_2, R4.Pin_0
  N7: R3.Pin_1, LED1.anode
